// Logisim project 8-bit microprocessor.circ as structural Verilog: 1 circuit, main circuit main
module main (
  input  in_1,
  input  in_2
);

  wire A, clk, Cp, E_R, EI, ER2, L_R, LC, LI, LM, LR0, LR1, LR2, nor_1_out, not_1_out, or_1_out,
       shift_register_1_p3, shift_register_1_p4, shift_register_1_p5, shift_register_1_p6,
       shift_register_1_p7, shift_register_1_p8, undriven;
  wire [3:0] MAR_q, PC_q_2;
  wire [4:0] adder_1_out, adder_2_out, controlled_buffer_1_out, rom_1_data;
  wire [7:0] adder_3_out, and_1_out, controlled_buffer_9_out, controlled_buffer_12_out, IR_q, R0_q, R1_q,
       R2_q, ram_1_dout;
  wire [7:4] PC_q;

  ROM #(.addrWidth(4), .dataWidth(5)) rom_1 (.addr(IR_q[7:4]), .data(rom_1_data));
  or or_1 (or_1_out, clk, in_2);
  Counter PC (
    .clr(in_1), .load(LC), .count(Cp), .clk(clk), .D(controlled_buffer_9_out), .Q({PC_q, PC_q_2}));  // open: up, carry
  RAM #(.addrWidth(4)) ram_1 (
    .addr(MAR_q), .we(L_R), .oe(1'b1), .clk(clk), .din(controlled_buffer_9_out), .dout(ram_1_dout));
  // Shift_Register #(.length(6)) shift_register_1: pin names not known; wires that end beside it: in_1, or_1_out, shift_register_1_p3, shift_register_1_p4, shift_register_1_p5, shift_register_1_p6, shift_register_1_p7, shift_register_1_p8, shift_register_1_p8
  or or_2 (shift_register_1_p3, in_2, shift_register_1_p8);
  Register #(.width(4)) MAR (.D(PC_q_2), .en(LM), .clk(clk), .Q(MAR_q), .clr(in_1));
  Register IR (.D(controlled_buffer_9_out), .en(LI), .clk(clk), .Q(IR_q), .clr(in_1));
  nor nor_1 (nor_1_out, undriven, shift_register_1_p4, shift_register_1_p5, shift_register_1_p6, shift_register_1_p7, shift_register_1_p8, shift_register_1_p8);
  assign controlled_buffer_1_out = nor_1_out ? {5{1'b1}} : 5'bz;  // Controlled_Buffer controlled_buffer_1
  assign controlled_buffer_1_out = undriven ? {5{1'b0}} : 5'bz;  // Controlled_Buffer controlled_buffer_2
  assign controlled_buffer_1_out = shift_register_1_p4 ? 5'b00001 : 5'bz;  // Controlled_Buffer controlled_buffer_3
  assign controlled_buffer_1_out = shift_register_1_p5 ? 5'b00010 : 5'bz;  // Controlled_Buffer controlled_buffer_4
  assign controlled_buffer_1_out = shift_register_1_p6 ? rom_1_data : 5'bz;  // Controlled_Buffer controlled_buffer_5
  assign controlled_buffer_1_out = shift_register_1_p7 ? rom_1_data : 5'bz;  // Controlled_Buffer controlled_buffer_6
  assign controlled_buffer_1_out = shift_register_1_p8 ? adder_1_out : 5'bz;  // Controlled_Buffer controlled_buffer_7
  Controlled_Buffer #(.width(5)) controlled_buffer_8 (.in(adder_2_out), .en(shift_register_1_p8));  // open: out
  assign controlled_buffer_9_out = E_R ? ram_1_dout : 8'bz;  // Controlled_Buffer controlled_buffer_9
  assign controlled_buffer_9_out = EI ? {4'b0000, IR_q[3:0]} : 8'bz;  // Controlled_Buffer controlled_buffer_10
  Adder #(.width(5)) adder_1 (.a(rom_1_data), .b(5'b00001), .out(adder_1_out));  // open: cin, cout
  Adder #(.width(5)) adder_2 (.b(5'b00010), .out(adder_2_out));  // open: a, cin, cout
  assign controlled_buffer_9_out = ER2 ? R2_q : 8'bz;  // Controlled_Buffer controlled_buffer_11
  ROM #(.addrWidth(5), .dataWidth(12)) rom_2 (
    .addr(controlled_buffer_1_out), .data({Cp, LR2, LM, E_R, L_R, LI, EI, LR0, LR1, A, LC, ER2}));
  Register R0 (.D(controlled_buffer_9_out), .en(LR0), .clk(clk), .Q(R0_q), .clr(in_1));
  Register R1 (.D(controlled_buffer_9_out), .en(LR1), .clk(clk), .Q(R1_q), .clr(in_1));
  Register R2 (.D(controlled_buffer_12_out), .en(LR2), .clk(clk), .Q(R2_q), .clr(in_1));
  assign controlled_buffer_12_out = not_1_out ? adder_3_out : 8'bz;  // Controlled_Buffer controlled_buffer_12
  Adder adder_3 (.a(R0_q), .b(R1_q), .out(adder_3_out));  // open: cin, cout
  assign and_1_out = R0_q & R1_q;  // AND_Gate and_1, 8 bits wide
  assign controlled_buffer_12_out = A ? and_1_out : 8'bz;  // Controlled_Buffer controlled_buffer_13
  not not_1 (not_1_out, A);
  _7_Segment_Display u_7_segment_display_1 ();  // open: g, f, a, b, e, d, c, dp
  // BCD_to_7_Segment_decoder bcd_to_7_segment_decoder_1: pin names not known
  // Binary_to_BCD_converter #(.binvalue(8)) binary_to_bcd_converter_1: pin names not known; wires that end beside it: R0_q
  _7_Segment_Display u_7_segment_display_2 ();  // open: g, f, a, b, e, d, c, dp
  // BCD_to_7_Segment_decoder bcd_to_7_segment_decoder_2: pin names not known
  // Binary_to_BCD_converter #(.binvalue(8)) binary_to_bcd_converter_2: pin names not known; wires that end beside it: R1_q
  _7_Segment_Display u_7_segment_display_3 ();  // open: g, f, a, b, e, d, c, dp
  // BCD_to_7_Segment_decoder bcd_to_7_segment_decoder_3: pin names not known
  // Binary_to_BCD_converter #(.binvalue(8)) binary_to_bcd_converter_3: pin names not known; wires that end beside it: R2_q
  _7_Segment_Display u_7_segment_display_4 ();  // open: g, f, a, b, e, d, c, dp
  _7_Segment_Display u_7_segment_display_5 ();  // open: g, f, a, b, e, d, c, dp
  // BCD_to_7_Segment_decoder bcd_to_7_segment_decoder_4: pin names not known
  // BCD_to_7_Segment_decoder bcd_to_7_segment_decoder_5: pin names not known; wires that end beside it: clk
  _7_Segment_Display u_7_segment_display_6 ();  // open: g, f, a, b, e, d, c, dp
  _7_Segment_Display u_7_segment_display_7 ();  // open: g, f, a, b, e, d, c, dp
  // BCD_to_7_Segment_decoder bcd_to_7_segment_decoder_6: pin names not known
  // BCD_to_7_Segment_decoder bcd_to_7_segment_decoder_7: pin names not known
  _7_Segment_Display u_7_segment_display_8 ();  // open: g, f, a, b, e, d, c, dp
  _7_Segment_Display u_7_segment_display_9 ();  // open: g, f, a, b, e, d, c, dp
  // BCD_to_7_Segment_decoder bcd_to_7_segment_decoder_8: pin names not known
  // BCD_to_7_Segment_decoder bcd_to_7_segment_decoder_9: pin names not known
  Clock clock_1 (.out(clk));

  // Other names for the same wires on the sheet: CLR = in_1; Set = in_2

  // Notes on the sheet:
  //   contents of rom_1 (hex, n*v repeats v):
  //   3 6 9 c f 12 15 18 1a
  //   contents of rom_2 (hex, n*v repeats v):
  //   200 800 140 220 910 0 220 908 0 400 0 0 220 881 0 11 0 0 220 908 0 404 0 0 220 881 0 222 22
endmodule
